# Fritzing sketch receiver (saved by Fritzing 0.9.1b)

parts:
  Parte1 = Arduino Uno (Rev3)
  JP1 = Header 4 [package=jst-4-pth]

nets:
  N1: Parte1.D2, JP1.2
  N2: Parte1.5V, JP1.1
  N3: Parte1.GND, JP1.4
