# Fritzing sketch transmitter (saved by Fritzing 0.9.1b)
perfboards: 1

parts:
  JP1 = Header 3 [package=screwterminal-3.5mm-3_lock.007s]
  Parte1 = FTDI Basic Programmer
  S2 = Pushbutton [package=THT]
  S3 = Pushbutton [package=THT]

nets:
  N1: JP1.1, Parte1.POWER
  N2: Parte1.GND, S2.leg0, S3.leg0

notes:
  program (0)
  Reset
